# Fritzing sketch 555 Speed Controller - Exhaust Fan (saved by Fritzing 0.9.3b)
breadboards: 1

parts:
  U1 = 555 Timer [package="DIP8 [THT]"]
  R1 = Resistor [tolerance=±5% resistance=1k package=THT]
  R2 = Trimmer Potentiometer [maximum_resistance=1kΩ package=THT]
  R3 = Resistor [tolerance=±5% resistance=4.7k package=THT]
  C1 = Ceramic Capacitor [capacitance=100nF package="100 mil [THT, multilayer]"]
  C2 = Electrolytic Capacitor [capacitance=1µF package="100 mil [THT, electrolytic]"]
  D1 = Rectifier Diode [part_number=1N4148 package="300 mil [THT]"]
  D2 = Rectifier Diode [part_number=1N4148 package="300 mil [THT]"]
  R4 = Resistor [tolerance=±5% resistance=500 package=THT]
  LED1 = LED - 5mm [color="Red (633nm)" package="5 mm [THT]"]
  J2 = 4-Pin Brushless DC Fan [part_number="4-Pin Fan" package=THT]

nets:
  GND: U1.Ground, C1.0, C2.-, LED1.cathode, J2.pin4
  N1: U1.Trigger, U1.Threshold, D1.anode
  N2: U1.Output, R2.wiper
  12V: U1.Reset, U1.Discharge, U1.Vcc_Supply_Voltage, R1.Pin_0, C2.+, R4.Pin_1, J2.pin1
  N3: R1.Pin_1, J2.pin2
  N4: R2.leg1, R3.Pin_0, D2.anode
  N5: R2.leg2, R3.Pin_1, D1.cathode
  N6: C1.1, D2.cathode
  N7: R4.Pin_0, LED1.anode

notes:
  Vcc
  CTRL
  TACH
  GND
