# Fritzing sketch Arduino Nano Speed Control - Exhaust Fan (saved by Fritzing 0.9.3b)
breadboards: 1

parts:
  Part1 = Arduino Nano (Rev3.0)
  Q1 = Basic FET N-Channel [part_number=IRF510 package="TO220 [THT]"]
  D1 = Rectifier Diode [part_number=1N4001 package="300 mil [THT]"]
  J1 = 4-Pin Brushless DC Fan [part_number="4-Pin Fan" package=THT]
  R1 = Trimmer Potentiometer [maximum_resistance=10kΩ package=THT]
  R5 = Resistor [tolerance=±5% resistance=500 package=THT]
  LED2 = LED - 5mm [color="Red (633nm)" package="5 mm [THT]"]

nets:
  GND: Part1.GND, Q1.source, R1.leg1, LED2.cathode
  N1: Part1.D9, Q1.gate
  12V: Part1.VIN, D1.cathode, J1.pin1, R5.Pin_1
  N2: Part1.5V, R1.leg2
  N3: Part1.A0, R1.wiper
  N4: Q1.drain, D1.anode, J1.pin4
  N5: R5.Pin_0, LED2.anode

notes:
  TACH
  CTRL
  Vcc
  GND
